# Fritzing sketch MintDuino Project 1 - SubTask 5 Final Circuit (saved by Fritzing 0.5.2b)
breadboards: 2

parts:
  U1 = atmega168 [package="DIP28 [THT]"]
  S2 = Pushbutton [package="[THT]"]
  S2_2 = Pushbutton [package="[THT]"]
  LED2 = green LED - 5mm [package="5 mm [THT]"]
  LED2_2 = green LED - 5mm [package="5 mm [THT]"]
  R1 = Resistor [resistance=100 package=THT]
  R1_2 = Resistor [resistance=100 package=THT]
  R1_3 = Resistor [resistance=100 package=THT]
  LED1 = yellow LED - 5mm [package="5 mm [THT]"]

nets:
  N1: U1.Pin_5, S2_2.Pin_3, S2_2.Pin_4, LED2_2.cathode, R1_2.Pin_1
  N2: U1.Pin_6, S2.Pin_3, S2.Pin_4, LED2.cathode, R1_3.Pin_1
  N3: U1.Pin_8, U1.Pin_22
  N4: U1.Pin_12, LED2.anode
  N5: U1.Pin_13, LED2_2.anode
  N6: U1.Pin_14, LED1.anode
  N7: S2.Pin_1, S2.Pin_2, S2_2.Pin_1, S2_2.Pin_2
  N8: R1.Pin_0, R1_2.Pin_0, R1_3.Pin_0
  N9: R1.Pin_1, LED1.cathode

notes:
  +5V
  GND
  MintDuino
  All Resistors 100ohm
  Are the bottom pins all off by one?
